# Fritzing sketch Drum Lights (saved by Fritzing 0.9.9b)

parts:
  C1 = Capacitor Polarized [package=cpol-radial-1000uf-63v]
  J1 = Power Jack [package=power_jack_pth]
  WeMos_D1_Mini1 = WeMos D1 Mini
  NRF24L01 = NRF24L01 [part_number=NRF24L01]

nets:
  N1: C1.+, J1.PWR, WeMos_D1_Mini1.5V
  GND: C1.-, J1.GND, WeMos_D1_Mini1.G, NRF24L01.GND
  3V3: WeMos_D1_Mini1.3V3, NRF24L01.VCC
  N2: WeMos_D1_Mini1.D2, NRF24L01.CE
  N3: WeMos_D1_Mini1.D5, NRF24L01.SCK
  N4: WeMos_D1_Mini1.D6, NRF24L01.MISO
  N5: WeMos_D1_Mini1.D7, NRF24L01.MOSI
  N6: WeMos_D1_Mini1.D8, NRF24L01.CSN
